// Logisim project final_circuit.circ as structural Verilog
module RAM_16x8 (
);

  Byte_Reg byte_reg_1 ();  // open: CS, RW, CLK, I, O
  Byte_Reg byte_reg_2 ();  // open: CS, RW, CLK, I, O
  Byte_Reg byte_reg_3 ();  // open: CS, RW, CLK, I, O
  Byte_Reg byte_reg_4 ();  // open: CS, RW, CLK, I, O
endmodule

module Byte_Reg (
  input  [7:0] I,
  input  CLK,
  input  RW,
  input  CS,
  output [7:0] O
);

  wire and_1_out, and_2_out;
  wire [7:0] controlled_buffer_1_out, R_0_q;

  assign controlled_buffer_1_out = and_1_out ? I : 8'bz;  // Controlled_Buffer controlled_buffer_1
  and and_1 (and_1_out, RW, CS);
  and and_2 (and_2_out, CS, ~RW);  // AND_Gate
  D_Flip_Flop R_4 (.D(controlled_buffer_1_out[4]), .clk(CLK), .Q(R_0_q[4]));  // open: Qn, preset, reset
  D_Flip_Flop R_5 (.D(controlled_buffer_1_out[5]), .clk(CLK), .Q(R_0_q[5]));  // open: Qn, preset, reset
  D_Flip_Flop R_6 (.D(controlled_buffer_1_out[6]), .clk(CLK), .Q(R_0_q[6]));  // open: Qn, preset, reset
  D_Flip_Flop R_7 (.D(controlled_buffer_1_out[7]), .clk(CLK), .Q(R_0_q[7]));  // open: Qn, preset, reset
  assign O = and_2_out ? R_0_q : 8'bz;  // Controlled_Buffer controlled_buffer_2
  D_Flip_Flop R_0 (.D(controlled_buffer_1_out[0]), .clk(CLK), .Q(R_0_q[0]));  // open: Qn, preset, reset
  D_Flip_Flop R_1 (.D(controlled_buffer_1_out[1]), .clk(CLK), .Q(R_0_q[1]));  // open: Qn, preset, reset
  D_Flip_Flop R_2 (.D(controlled_buffer_1_out[2]), .clk(CLK), .Q(R_0_q[2]));  // open: Qn, preset, reset
  D_Flip_Flop R_3 (.D(controlled_buffer_1_out[3]), .clk(CLK), .Q(R_0_q[3]));  // open: Qn, preset, reset
endmodule
